// Logisim project CPUMk1.circ as structural Verilog: 3 circuits, main circuit main
module main (
  input  [15:0] Extended_Input,
  input  Reset,
  output [15:0] out_3
);

  wire Clock_out;
  wire [15:0] cpu_1_memory_selector, rom_1_data;

  Clock Clock (.out(Clock_out));
  CPU cpu_1 (
    .Ext_input(Extended_Input), .Mem_input(rom_1_data), .RST(Reset), .CLK(Clock_out),
    .Memory_Selector(cpu_1_memory_selector), .Output(out_3));
  ROM #(.addrWidth(16), .dataWidth(16)) rom_1 (.addr(cpu_1_memory_selector), .data(rom_1_data));  // open: sel

  // Notes on the sheet:
  //   contents of rom_1 (hex, n*v repeats v):
  //   0 7 2 3 7 5 d f 11
endmodule

module ALU (
  input  [2:0] Operation_Select,
  input  [15:0] Input_A,
  input  [15:0] Input_B,
  output [15:0] Outut_C
);

  wire [15:0] adder_1_out, adder_2_out, adder_3_out, and_1_out, or_1_out, subtractor_1_out;

  Adder #(.width(16)) adder_1 (.a(Input_A), .b(16'h1), .out(adder_1_out));  // open: cin, cout
  Adder #(.width(16)) adder_2 (.a(Input_B), .b(16'h1), .out(adder_2_out));  // open: cin, cout
  Adder #(.width(16)) adder_3 (.a(Input_A), .b(Input_B), .out(adder_3_out));  // open: cin, cout
  Subtractor #(.width(16)) subtractor_1 (.a(Input_A), .b(Input_B), .out(subtractor_1_out));  // open: bin, bout
  assign and_1_out = Input_A & Input_B;  // AND_Gate and_1, 16 bits wide
  assign or_1_out = Input_A | Input_B;  // OR_Gate or_1, 16 bits wide
  Multiplexer #(.select(3), .width(16)) multiplexer_1 (
    .in0(Input_A), .in1(Input_B), .in2(and_1_out), .in3(or_1_out), .in4(adder_1_out), .in5(adder_2_out),
    .in6(adder_3_out), .in7(subtractor_1_out), .out(Outut_C), .sel(Operation_Select));  // open: en
endmodule

module CPU (
  input  [15:0] Ext_input,
  input  [15:0] Mem_input,
  input  RST,
  input  CLK,
  output [15:0] Memory_Selector,
  output [15:0] Output
);

  wire Write_A, Write_B, Write_IC, Write_Mem, Write_Out;
  wire [1:0] rom_1_data_3;
  wire [2:0] rom_1_data_2;
  wire [6:0] MPC_q, multiplexer_2_out;
  wire [7:0] rom_1_data;
  wire [15:0] A_q, B_q, Data_Bus, Mem_q, multiplexer_1_out;

  Register #(.width(16)) Mem (.D(Mem_input), .Q(Mem_q), .clk(Write_Mem), .clr(RST));  // open: en
  Register #(.width(16)) IC (.D(Data_Bus), .Q(Memory_Selector), .clk(Write_IC), .clr(RST));  // open: en
  Register #(.width(16)) A (.D(Data_Bus), .Q(A_q), .clk(Write_A), .clr(RST));  // open: en
  Register #(.width(16)) B (.D(Data_Bus), .Q(B_q), .clk(Write_B), .clr(RST));  // open: en
  Register #(.width(16)) Out (.D(Data_Bus), .Q(Output), .clk(Write_Out), .clr(RST));  // open: en
  ALU alu_1 (.Operation_Select(rom_1_data_2), .Input_A(A_q), .Input_B(multiplexer_1_out), .Outut_C(Data_Bus));
  Multiplexer #(.select(2), .width(16), .disabled(0), .enable("false")) multiplexer_1 (
    .in0(B_q), .in1(Mem_q), .in2(Memory_Selector), .in3(Ext_input), .out(multiplexer_1_out),
    .sel(rom_1_data_3));
  Multiplexer #(.width(7), .disabled(0), .enable("false")) multiplexer_2 (
    .in0(Mem_q[6:0]), .in1(rom_1_data[6:0]), .out(multiplexer_2_out), .sel(rom_1_data[7]));
  Register #(.width(7)) MPC (.D(multiplexer_2_out), .Q(MPC_q), .clk(CLK), .clr(RST));  // open: en
  ROM #(.addrWidth(7), .dataWidth(18)) rom_1 (
    .addr(MPC_q),
    .data({Write_Mem, Write_Out, Write_B, Write_A, Write_IC, rom_1_data_3, rom_1_data_2, rom_1_data}));  // open: sel

  // Other names for the same wires on the sheet: Reset = RST

  // Notes on the sheet:
  //   contents of rom_1 (hex, n*v repeats v):
  //   1581 3582 20000 84 8080 186 4180 1588 3589 2098a 4980 68c 4680 78e 4780 90 10080 92 20000
endmodule
